# Fritzing sketch AutoPetFeedCircuit (saved by Fritzing 0.9.4)
breadboards: 1

parts:
  부품1 = Arduino Mega 2560 (Rev3)
  J1 = Basic Servo
  J2 = Basic Servo
  J3 = Basic Servo
  부품2 = Bluetooth HC-06
  ZS-042_RTC1 = ZS-042 RTC Module
  부품3 = HX711 Weighing Sensor Module
  J4 = Piezo Speaker

nets:
  N1: 부품1.D21/SCL, ZS-042_RTC1.SCL
  N2: 부품1.D20/SDA, ZS-042_RTC1.SDA
  N3: 부품1.D19/RX1, 부품2.TXD
  N4: 부품1.D18/TX1, 부품2.RXD
  GND: 부품1.GND, J1.gnd, J2.gnd, J3.gnd, 부품2.GND, ZS-042_RTC1.GND, 부품3.GND, J4.pin1
  N5: 부품1.D13_PWM, J4.pin2
  N6: 부품1.D10_PWM, J3.pulse
  N7: 부품1.D9_PWM, J2.pulse
  N8: 부품1.D8_PWM, J1.pulse
  VCC: 부품1.VIN, J1.vcc, J2.vcc, 부품2.VCC, ZS-042_RTC1.VCC, 부품3.VCC
  N9: 부품1.D6_PWM, 부품3.DO/RX
  N10: 부품1.D7_PWM, 부품3.CK/TX
