# Fritzing sketch HeartBeatCircuit (saved by Fritzing 0.9.4)
breadboards: 1

parts:
  MH-ET_LIVE_ESP32_DEVKIT1 = MH-ET LIVE ESP32 DEVKIT 38 pins
  M1 = MAX30102
  U1 = Vibration Motor- ROB-08449 [package=vibe-motor-10mm]
  Q1 = NPN-Transistor [package="TO92 [THT]"]
  R1 = Resistor [tolerance=±5% resistance=220 package="0805 [SMD]"]
  D1 = Diode [package=diode-1n4001]

nets:
  5V: MH-ET_LIVE_ESP32_DEVKIT1.5V, M1.VIN, U1.-, D1.C
  N1: MH-ET_LIVE_ESP32_DEVKIT1.IO23, R1.Pin_0
  N2: MH-ET_LIVE_ESP32_DEVKIT1.IO22, M1.SCL
  N3: MH-ET_LIVE_ESP32_DEVKIT1.IO21, M1.SDA
  N4: MH-ET_LIVE_ESP32_DEVKIT1.GND#70, M1.GND, Q1.E
  N5: U1.+, Q1.C, D1.A
  N6: Q1.B, R1.Pin_1

custom parts:
  MH-ET LIVE ESP32 DEVKIT 38 pins: http://mh.nodebb.com/topic/2/mh-et-live-esp32-devkit
  MAX30102: Oximeter module using the MAX30102 chip. You may wish to read (and check your module) this post on power problems with these modules: https://reedpaper.wordpress.com/2018/08/22/pulse-oximeter-max30100-max30102-how-to-fix-wrong-board/ . As usual, if you want the mounting holes in pcb, you need to drag a hole over the pad in silkscreen to actually drill the hole (by default they are not drilled)
